# Fritzing sketch teatrino-interfaccia (saved by Fritzing 0.9.3b)
circuit board: 6.8486cm x 5.30578cm
breadboards: 1

parts:
  S1 = Pushbutton [package="[THT]"]
  S2 = Pushbutton [package="[THT]"]
  S3 = Pushbutton [package="[THT]"]
  S4 = Pushbutton [package="[THT]"]
  LED1 = LED - 5mm [color="White (4500K)" package="5 mm [THT]"]
  S5 = Pushbutton [package="[THT]"]
  R1 = Resistor [tolerance=±5% resistance=1k package=THT]
  J1 = Basic Servo
  R2 = Resistor [tolerance=±5% resistance=1k package=THT]
  R3 = Resistor [tolerance=±5% resistance=1k package=THT]
  LED4 = LED - 5mm [color="Red (633nm)" package="5 mm [THT]"]
  R5 = Resistor [tolerance=±5% resistance=1k package=THT]
  R6 = Resistor [tolerance=±5% resistance=1k package=THT]
  R7 = Resistor [tolerance=±5% resistance=1k package=THT]
  R8 = Resistor [tolerance=±5% resistance=1k package=THT]
  LED3 = RGB LED (com. cathode, rbg) [package="5 mm [THT]"]
  Power_5vdc = Power plug
  Q2 = NPN-Transistor [part_number=TIP120 package="TO92 [THT]"]
  R10 = Resistor [tolerance=±5% resistance=1k package=THT]
  Q1 = NPN-Transistor [part_number=TIP120 package="TO92 [THT]"]
  R9 = Resistor [tolerance=±5% resistance=1k package=THT]
  LED2 = RGB LED (com. cathode, rbg) [package="5 mm [THT]"]
  R4 = Resistor [tolerance=±5% resistance=1k package=THT]
  Interfaccia = Arduino Uno (Rev3)

nets:
  GND: S1.Pin_1, S1.Pin_2, S2.Pin_1, S2.Pin_2, S3.Pin_1, S3.Pin_2, S4.Pin_1, S4.Pin_2, LED1.cathode, S5.Pin_1, S5.Pin_2, J1.gnd, LED4.cathode, LED3.common_cathode, Power_5vdc.GND, Q2.E, Q1.E, LED2.common_cathode, Interfaccia.GND
  N1: S1.Pin_3, S1.Pin_4, Interfaccia.A0
  N2: S2.Pin_3, S2.Pin_4, Interfaccia.A1
  N3: S3.Pin_3, S3.Pin_4, Interfaccia.A2
  N4: S4.Pin_3, S4.Pin_4, Interfaccia.A3
  N5: LED1.anode, R1.Pin_0
  N6: S5.Pin_3, S5.Pin_4, Interfaccia.D7
  N7: R1.Pin_1, R9.Pin_1, Interfaccia.D8
  VCC: J1.vcc, Power_5vdc.VCC, Interfaccia.5V
  N8: J1.pulse, Interfaccia.D4
  N9: R2.Pin_0, LED2.red_anode
  N10: R2.Pin_1, Interfaccia.D3_PWM
  N11: R3.Pin_0, LED2.blue_anode
  N12: R3.Pin_1, Interfaccia.D6_PWM
  N13: LED4.anode, R5.Pin_0
  N14: R5.Pin_1, R10.Pin_1, Interfaccia.D0/RX
  N15: R6.Pin_0, LED3.green_anode
  N16: R6.Pin_1, Interfaccia.D10_PWM/SS
  N17: R7.Pin_0, LED3.blue_anode
  N18: R7.Pin_1, Interfaccia.D11_PWM/MOSI
  N19: R8.Pin_0, LED3.red_anode
  N20: R8.Pin_1, Interfaccia.D9_PWM
  N21: Q2.B, R10.Pin_0
  N22: Q1.B, R9.Pin_0
  N23: LED2.green_anode, R4.Pin_0
  N24: R4.Pin_1, Interfaccia.D5_PWM

notes:
  apri
  chiudi
  FCa
  FCc
  Luci Fronte
  Luci Scena
  i2c
  Luci Fondale
  H-Bridge
  Vin 5V
  Sparabolle
  alimentazione e sparabolle
  LED STRIP 12V Luci Fronte

// code stored in the sketch: teatrino-interfaccia.ino
/*
   Gruppo "cena mensile del martedi' all'ostello" presenta:
   INTERFACCIA automazione per teatrino marionette/burattini
   scheda: Arduino Uno/Duemilanove/simili (20 in-out)
*/


// -- Sipario
#define tendaApriPin 12 // attiva un lato dell'H-Bridge
#define tendaChiudiPin 13 // attiva l'altro lato dell'H-Bridge
#define tendaApriPulsPin A0 // pulsante apertura
#define tendaChiudiPulsPin A1 // pulsante chiusura
#define tendaFinecorsaApriPin A2 // segnala completa apertura
#define tendaFinecorsaChiudiPin A3 // segnala completa chiusura
bool statoFinaleTenda = HIGH; // corrisponde a tenda chiusa

// -- Luci fronte
#define luciFrontePin 7 // con circuito transistor per 12V striscia LED bianco
#define luciFrontePulsPin 8 // pulsante luci fronte
bool statoLuciFronte = LOW; // luci spente

// -- Luci di scena
#define luciScenaRossoPin 3 // PWM -> collegato a circuito transistor per 12V LED rosso
#define luciScenaVerdePin 5 // PWM -> collegato a circuito transistor per 12V LED verde
#define luciScenaBluPin 6 // PWM -> collegato a circuito transistor per 12V LED blu
byte coloreLuciScena[3] = {0, 0, 0}; // valori RGB per luci spente

// -- Fondale
#define luciFondaleRossoPin 9 // PWM -> collegato a circuito transistor per 12V LED rosso
#define luciFondaleVerdePin 10 // PWM -> collegato a circuito transistor per 12V LED verde
#define luciFondaleBluPin 11 // PWM -> collegato a circuito transistor per 12V LED blu
byte coloreLuciFondale[3] = {0, 0, 0}; // valori RGB per luci spente
#define servoFondalePin 4 // pin del servo che fa girare il fondale
bool avanzaServoFondale = LOW;

// -- Occhio di bue
#define XservoOcchioPin 1 // pin del servo asse x
#define YservoOcchioPin 2// pin del servo asse y
byte posizioneOcchio[2] = {128, 128}; // valori a mezza scala per posizione centrale (dipende dal servo)

// -- Sparabolle
#define bollePin 0  // circuito con transistor che alimenta la sparabolle elettrica
bool statoBolle = LOW;

// -- Comunicazione con controller
#define i2cSDA A4 // dati
#define i2cSDC A5 // clock

// LIBRERIE
#include <Wire.h>

#include <Servo.h>
Servo servoFondale;  // crea l'oggetto servoFondale
Servo servoOcchioX;  // crea l'oggetto servoOcchioX
Servo servoOcchioY;  // crea l'oggetto servoOcchioY

// ------------------------------------------------

void setup() {
  // -- Sipario
  pinMode(tendaApriPin, OUTPUT);
  pinMode(tendaChiudiPin, OUTPUT);
  pinMode(tendaApriPulsPin, INPUT_PULLUP);
  pinMode(tendaChiudiPulsPin, INPUT_PULLUP);
  pinMode(tendaFinecorsaApriPin, INPUT_PULLUP);
  pinMode(tendaFinecorsaChiudiPin, INPUT_PULLUP);

  // -- Luci fronte
  pinMode(luciFrontePin, OUTPUT);
  pinMode(luciFrontePulsPin, INPUT_PULLUP);

  // -- Luci di scena
  pinMode(luciScenaRossoPin, OUTPUT); // per completezza, ma inutili usando analogWrite
  pinMode(luciScenaVerdePin, OUTPUT);
  pinMode(luciScenaBluPin, OUTPUT);

  // -- Fondale
  pinMode(luciFondaleRossoPin, OUTPUT); // per completezza, ma inutili usando analogWrite
  pinMode(luciFondaleVerdePin, OUTPUT);
  pinMode(luciFondaleBluPin, OUTPUT);

  servoFondale.attach(servoFondalePin);

  // -- Occhio di bue
  servoOcchioX.attach(XservoOcchioPin);
  servoOcchioY.attach(YservoOcchioPin);

  // -- Sparabolle
  pinMode(bollePin, OUTPUT);

  // -- Comunicazione, con controller pensato come master
  Wire.begin(8); // unisciti al bus i2c con indirizzo 8
  Wire.onReceive(riceviControllo); // chiama riceviControllo se ricevi da master i2c
  Wire.onRequest(trasmettiDati);  // eseguita ogni volta che il Controllore/Master richiede dati


  // !! DEBUG !!
  Serial.begin(9600);           // avvia supporto seriale
}


void loop() {
  sipario();
  apriSipario();
  chiudiSipario();
  luciFronte();
  luciScena();
  fondale();
  // comunicazione();
  // occhio();
  sparabolle();
}


// Sipario
void sipario() {
  if (digitalRead(tendaApriPulsPin) == LOW) statoFinaleTenda = LOW;
  if (digitalRead(tendaChiudiPulsPin) == LOW) statoFinaleTenda = HIGH;
}

void apriSipario() {
  if (digitalRead(tendaFinecorsaApriPin) == HIGH && statoFinaleTenda == LOW) {
    digitalWrite (tendaApriPin, HIGH);
  }
  else {
    digitalWrite (tendaApriPin, LOW);
  }
}

void chiudiSipario() {
  if (digitalRead(tendaFinecorsaChiudiPin) == HIGH && statoFinaleTenda == HIGH) {
    digitalWrite (tendaChiudiPin, HIGH);
  }
  else {
    digitalWrite (tendaChiudiPin, LOW);
  }
}


// Luci fronte
void luciFronte() {
  if (digitalRead(luciFrontePulsPin) == LOW) { // il pulsante e' stato schiacciato
    statoLuciFronte = !statoLuciFronte; // inverte lo stato della luce
    digitalWrite(luciFrontePin, statoLuciFronte);
    delay(100); // per evitare accensioni-spegnimenti in serie
  }
}


// Luci di Scena
void luciScena() {
  analogWrite (luciScenaRossoPin, coloreLuciScena[0]);
  analogWrite (luciScenaVerdePin, coloreLuciScena[1]);
  analogWrite (luciScenaBluPin, coloreLuciScena[2]);
}

// Fondale
void fondale() {
  analogWrite (luciFondaleRossoPin, coloreLuciFondale[0]);
  analogWrite (luciFondaleVerdePin, coloreLuciFondale[1]);
  analogWrite (luciFondaleBluPin, coloreLuciFondale[2]);

  if (avanzaServoFondale == HIGH) avanzaFondale();
}

void avanzaFondale() {
  servoFondale.write(20); // fa avanzare il servo di un po'
  delay(15); // aspetta un momento per il movimento
  avanzaServoFondale = LOW; // resetta variabile
}

// Comunicazione
void comunicazione() {}

void trasmettiDati() { // invia lo stato delle variabili al master
  Wire.write(statoFinaleTenda);
  Wire.write(digitalRead(tendaFinecorsaApriPin)); // segnala completa apertura
  Wire.write(digitalRead(tendaFinecorsaChiudiPin)); // segnala completa chiusura
  Wire.write(statoLuciFronte);
  Wire.write(coloreLuciScena[0]);
  Wire.write(coloreLuciScena[1]);
  Wire.write(coloreLuciScena[2]);
  Wire.write(coloreLuciFondale[0]);
  Wire.write(coloreLuciFondale[1]);
  Wire.write(coloreLuciFondale[2]);
  Wire.write(avanzaServoFondale);
  Wire.write(posizioneOcchio[0]);
  Wire.write(posizioneOcchio[1]);
  Wire.write(statoBolle);
}

void riceviControllo(int r) {
  while (1 < Wire.available()) { // loop through all but the last
    statoFinaleTenda = Wire.read();
    statoLuciFronte = Wire.read();
    coloreLuciScena[0] = Wire.read();
    coloreLuciScena[1] = Wire.read();
    coloreLuciScena[2] = Wire.read();
    coloreLuciFondale[0] = Wire.read();
    coloreLuciFondale[1] = Wire.read();
    coloreLuciFondale[2] = Wire.read();
    avanzaServoFondale = Wire.read();
    posizioneOcchio[0] = Wire.read();
    posizioneOcchio[1] = Wire.read();
    statoBolle = Wire.read();
  }
}

// Occhio di bue
void occhio() {}

// Sparabolle
void sparabolle() {
  // digitalWrite(bollePin, HIGH);
}

// code stored in the sketch: teatrino.ino
/*
   Gruppo "cena mensile del martedi' all'ostello" presenta:
   INTERFACCIA automazione per teatrino marionette/burattini
   scheda: Arduino Uno/Duemilanove/simili (20 in-out)
*/

/*
   CONTROLLER (con attiny84 che ha 10-11 pin disponibili)
   interruttore ON-OFF -> chiude l'alimentazione
   display 4 linee per 16 caratteri -> 6 DO
   potenziometro per modifica valori RGB -> 1 AI
   pulsante per conferma valori immessi -> 1 DI
   i2c -> 2 DO
*/


// -- Sipario
#define tendaApriPin 12 // attiva un lato dell'H-Bridge
#define tendaChiudiPin 13 // attiva l'altro lato dell'H-Bridge
#define tendaApriPulsPin A0 // pulsante apertura
#define tendaChiudiPulsPin A1 // pulsante chiusura
#define tendaFinecorsaApriPin A2 // segnala completa apertura
#define tendaFinecorsaChiudiPin A3 // segnala completa chiusura
bool statoFinaleTenda = HIGH; // corrisponde a tenda chiusa

// -- Luci fronte
#define luciFrontePin 7 // con circuito transistor per 12V striscia LED bianco
#define luciFrontePulsPin 8 // pulsante luci fronte
bool statoLuciFronte = LOW; // luci spente

// -- Luci di scena
#define luciScenaRossoPin 3 // PWM -> collegato a circuito transistor per 12V LED rosso
#define luciScenaVerdePin 5 // PWM -> collegato a circuito transistor per 12V LED verde
#define luciScenaBluPin 6 // PWM -> collegato a circuito transistor per 12V LED blu
byte coloreLuciScena[3] = {0, 100, 0}; // valori RGB per luci spente

// -- Fondale
#define luciFondaleRossoPin 9 // PWM -> collegato a circuito transistor per 12V LED rosso
#define luciFondaleVerdePin 10 // PWM -> collegato a circuito transistor per 12V LED verde
#define luciFondaleBluPin 11 // PWM -> collegato a circuito transistor per 12V LED blu
byte coloreLuciFondale[3] = {0, 0, 100}; // valori RGB per luci spente
#define servoFondalePin 4 // pin del servo che fa girare il fondale
bool avanzaServoFondale = LOW;
// -- Occhio di bue
#define XservoOcchioPin 1 // pin del servo asse x
#define YservoOcchioPin 2// pin del servo asse y
byte posizioneOcchio[2] = {128, 128}; // valori a mezza scala per posizione centrale (dipende dal servo)

// -- Sparabolle
#define bollePin 0  // circuito con transistor che alimenta la sparabolle elettrica
bool statoBolle = LOW;

// -- Comunicazione con controller
#define i2cSDA A4 // dati
#define i2cSDC A5 // clock

// LIBRERIE
#include <Wire.h>

#include <Servo.h>
Servo servoFondale;  // crea l'oggetto servoFondale
Servo servoOcchioX;  // crea l'oggetto servoOcchioX
Servo servoOcchioY;  // crea l'oggetto servoOcchioY

// ------------------------------------------------

void setup() {
  // -- Sipario
  pinMode(tendaApriPin, OUTPUT);
  pinMode(tendaChiudiPin, OUTPUT);
  pinMode(tendaApriPulsPin, INPUT_PULLUP);
  pinMode(tendaChiudiPulsPin, INPUT_PULLUP);
  pinMode(tendaFinecorsaApriPin, INPUT_PULLUP);
  pinMode(tendaFinecorsaChiudiPin, INPUT_PULLUP);

  // -- Luci fronte
  pinMode(luciFrontePin, OUTPUT);
  pinMode(luciFrontePulsPin, INPUT_PULLUP);

  // -- Luci di scena
  pinMode(luciScenaRossoPin, OUTPUT); // per completezza, ma inutili usando analogWrite
  pinMode(luciScenaVerdePin, OUTPUT);
  pinMode(luciScenaBluPin, OUTPUT);

  // -- Fondale
  pinMode(luciFondaleRossoPin, OUTPUT); // per completezza, ma inutili usando analogWrite
  pinMode(luciFondaleVerdePin, OUTPUT);
  pinMode(luciFondaleBluPin, OUTPUT);

  servoFondale.attach(servoFondalePin);

  // -- Occhio di bue
  servoOcchioX.attach(XservoOcchioPin);
  servoOcchioY.attach(YservoOcchioPin);

  // -- Sparabolle
  pinMode(bollePin, OUTPUT);

  // -- Comunicazione, con controller pensato come master
  Wire.begin(8); // unisciti al bus i2c con indirizzo 8
  Wire.onReceive(riceviControllo); // chiama riceviControllo se ricevi da master i2c
  Wire.onRequest(trasmettiDati);  // eseguita ogni volta che il Controllore/Master richiede dati


  // !! DEBUG !!
  Serial.begin(9600);           // avvia supporto seriale
}


void loop() {
  sipario();
  apriSipario();
  chiudiSipario();
  luciFronte();
  luciScena();
  fondale();
  // comunicazione();
  // occhio();
  sparabolle();
}


// Sipario
void sipario() {
  if (digitalRead(tendaApriPulsPin) == LOW) statoFinaleTenda = LOW;
  if (digitalRead(tendaChiudiPulsPin) == LOW) statoFinaleTenda = HIGH;
}

void apriSipario() {
  if (digitalRead(tendaFinecorsaApriPin) == HIGH && statoFinaleTenda == LOW) {
    digitalWrite (tendaApriPin, HIGH);
  }
  else {
    digitalWrite (tendaApriPin, LOW);
  }
}

void chiudiSipario() {
  if (digitalRead(tendaFinecorsaChiudiPin) == HIGH && statoFinaleTenda == HIGH) {
    digitalWrite (tendaChiudiPin, HIGH);
  }
  else {
    digitalWrite (tendaChiudiPin, LOW);
  }
}


// Luci fronte
void luciFronte() {
  if (digitalRead(luciFrontePulsPin) == LOW) { // il pulsante e' stato schiacciato
    statoLuciFronte = !statoLuciFronte; // inverte lo stato della luce
    digitalWrite(luciFrontePin, statoLuciFronte);
    delay(100); // per evitare accensioni-spegnimenti in serie
  }
}


// Luci di Scena
void luciScena() {
  analogWrite (luciScenaRossoPin, coloreLuciScena[0]);
  analogWrite (luciScenaVerdePin, coloreLuciScena[1]);
  analogWrite (luciScenaBluPin, coloreLuciScena[2]);
}

// Fondale
void fondale() {
  analogWrite (luciFondaleRossoPin, coloreLuciFondale[0]);
  analogWrite (luciFondaleVerdePin, coloreLuciFondale[1]);
  analogWrite (luciFondaleBluPin, coloreLuciFondale[2]);

  if (avanzaServoFondale == HIGH) avanzaFondale();
}

void avanzaFondale() {
  servoFondale.write(20); // fa avanzare il servo di un po'
  delay(15); // aspetta un momento per il movimento
  avanzaServoFondale = LOW; // resetta variabile
}

// Comunicazione
void comunicazione() {}

void trasmettiDati() { // invia lo stato delle variabili al master
  Wire.write(statoFinaleTenda);
  Wire.write(digitalRead(tendaFinecorsaApriPin)); // segnala completa apertura
  Wire.write(digitalRead(tendaFinecorsaChiudiPin)); // segnala completa chiusura
  Wire.write(statoLuciFronte);
  Wire.write(coloreLuciScena[0]);
  Wire.write(coloreLuciScena[1]);
  Wire.write(coloreLuciScena[2]);
  Wire.write(coloreLuciFondale[0]);
  Wire.write(coloreLuciFondale[1]);
  Wire.write(coloreLuciFondale[2]);
  Wire.write(avanzaServoFondale);
  Wire.write(posizioneOcchio[0]);
  Wire.write(posizioneOcchio[1]);
  Wire.write(statoBolle);
}

void riceviControllo(int r) {
  while (1 < Wire.available()) { // loop through all but the last
    statoFinaleTenda = Wire.read();
    statoLuciFronte = Wire.read();
    coloreLuciScena[0] = Wire.read();
    coloreLuciScena[1] = Wire.read();
    coloreLuciScena[2] = Wire.read();
    coloreLuciFondale[0] = Wire.read();
    coloreLuciFondale[1] = Wire.read();
    coloreLuciFondale[2] = Wire.read();
    avanzaServoFondale = Wire.read();
    posizioneOcchio[0] = Wire.read();
    posizioneOcchio[1] = Wire.read();
    statoBolle = Wire.read();
  }
}

// Occhio di bue
void occhio() {}

// Sparabolle
void sparabolle() {
  // digitalWrite(bollePin, HIGH);
}
